// Logisim project Project2.circ as structural Verilog: 4 circuits, main circuit main
module part2 (
  input  [3:0] GPRegSel,
  input  [1:0] GPFunSel,
  input  [1:0] OutBSel,
  input  MuxCSel,
  input  [3:0] ALUFunSel,
  input  [1:0] OutASel,
  input  [1:0] MuxASel,
  input  [2:0] ARRegSel,
  input  [1:0] OutDSel,
  input  [1:0] ARFunSel,
  input  [1:0] OutCSel,
  input  [1:0] MuxBSel,
  input  L_prime__H,
  input  E,
  input  [1:0] IRFunSel,
  input  STR,
  input  CLK,
  output Z,
  output [15:0] IROut
);

  wire zcno_reg_1_c_out;
  wire [3:0] alu_1_outflag;
  wire [7:0] alu_1_outalu, multiplexer_1_out, multiplexer_2_out, multiplexer_3_out,
       n8_bit_address_registers_1_out_c, n8_bit_address_registers_1_out_d,
       n8_bit_general_purpose_registers_1_out_a, n8_bit_general_purpose_registers_1_out_b, ram_1_data;

  Multiplexer #(.select(2), .width(8), .enable("false")) multiplexer_1 (
    .in0(IROut[7:0]), .in1(ram_1_data), .in2(n8_bit_address_registers_1_out_c), .in3(alu_1_outalu),
    .out(multiplexer_1_out), .sel(MuxASel));
  Multiplexer #(.select(2), .width(8), .enable("false")) multiplexer_2 (
    .in1(IROut[7:0]), .in2(ram_1_data), .in3(alu_1_outalu), .out(multiplexer_2_out), .sel(MuxBSel));  // open: in0
  _16_bit_IR_register u_16_bit_ir_register_1 (
    .CLK(CLK), .E(E), .I(ram_1_data), .L_prime___H(L_prime__H), .FunSel(IRFunSel), .IRout(IROut));
  _8_bit_general_purpose_registers u_8_bit_general_purpose_registers_1 (
    .FunSel(GPFunSel), .I(multiplexer_1_out), .Out_A(n8_bit_general_purpose_registers_1_out_a),
    .Out_B(n8_bit_general_purpose_registers_1_out_b), .CLK(CLK), .RegSel(GPRegSel), .OutASel(OutASel),
    .OutBSel(OutBSel));
  Multiplexer #(.width(8), .enable("false")) multiplexer_3 (
    .in0(n8_bit_address_registers_1_out_c), .in1(n8_bit_general_purpose_registers_1_out_a),
    .out(multiplexer_3_out), .sel(MuxCSel));
  _8_bit_address_registers u_8_bit_address_registers_1 (
    .FunSel(ARFunSel), .I(multiplexer_2_out), .Out_C(n8_bit_address_registers_1_out_c),
    .Out_D(n8_bit_address_registers_1_out_d), .CLK(CLK), .RegSel(ARRegSel), .OutCSel(OutCSel),
    .OutDSel(OutDSel));
  ZCNO_REG zcno_reg_1 (.OutFlag(alu_1_outflag), .C_OUT(zcno_reg_1_c_out), .CLK(CLK), .Z_OUT(Z));
  ALU alu_1 (
    .FunSel(ALUFunSel), .OutALU(alu_1_outalu), .C_IN(zcno_reg_1_c_out), .A_INPUT(multiplexer_3_out),
    .B_INPUT(n8_bit_general_purpose_registers_1_out_b), .OutFlag(alu_1_outflag));
  RAM #(.bus("separate")) ram_1 (
    .addr(n8_bit_address_registers_1_out_d), .din(alu_1_outalu), .data(ram_1_data), .str(STR), .clk(CLK));  // open: sel, ld, clr
endmodule

module main (
  input  [7:0] A,
  input  [7:0] B,
  input  [3:0] FunSel,
  output [3:0] OutFlag,
  output [7:0] OutAlu
);

  wire clock_1_out, zcno_reg_1_c_out;

  Hex_Digit_Display hex_digit_display_1 (.value(A[7:4]));  // open: dp
  Hex_Digit_Display hex_digit_display_2 (.value(B[7:4]));  // open: dp
  Hex_Digit_Display hex_digit_display_3 (.value(A[3:0]));  // open: dp
  Hex_Digit_Display hex_digit_display_4 (.value(B[3:0]));  // open: dp
  ZCNO_REG zcno_reg_1 (.OutFlag(OutFlag), .C_OUT(zcno_reg_1_c_out), .CLK(clock_1_out));  // open: Z_OUT
  ALU alu_1 (.FunSel(FunSel), .OutALU(OutAlu), .C_IN(zcno_reg_1_c_out), .A_INPUT(A), .B_INPUT(B), .OutFlag(OutFlag));
  Clock clock_1 (.out(clock_1_out));
  Hex_Digit_Display hex_digit_display_5 (.value(OutAlu[7:4]));  // open: dp
  Hex_Digit_Display hex_digit_display_6 (.value(OutAlu[3:0]));  // open: dp

  // Notes on the sheet:
  //   Input A
  //   Input B
  //   OutALU
endmodule

module ALU (
  input  [7:0] A_INPUT,
  input  [7:0] B_INPUT,
  input  [3:0] FunSel,
  input  C_IN,
  output [7:0] OutALU,
  output [3:0] OutFlag
);

  wire adder_1_cout, and_2_out, and_3_out, subtractor_1_bout, subtractor_2_bout, xnor_1_out, xnor_2_out,
       xor_2_out, xor_3_out, xor_4_out, xor_5_out;
  wire [7:0] adder_1_out, and_1_out, not_1_out, not_2_out, or_1_out, shifter_1_out, shifter_2_out,
       shifter_3_out, shifter_4_out, subtractor_1_out, subtractor_2_out, xor_1_out;

  assign not_1_out = ~A_INPUT;  // NOT_Gate not_1, 8 bits wide
  Adder adder_1 (.a(A_INPUT), .b(B_INPUT), .out(adder_1_out), .cin(1'b0), .cout(adder_1_cout));
  Subtractor subtractor_1 (.a(B_INPUT), .b(A_INPUT), .out(subtractor_1_out), .bout(subtractor_1_bout));  // open: bin
  Subtractor subtractor_2 (.a(A_INPUT), .b(B_INPUT), .out(subtractor_2_out), .bout(subtractor_2_bout));  // open: bin
  assign and_1_out = A_INPUT & B_INPUT;  // AND_Gate and_1, 8 bits wide
  assign or_1_out = A_INPUT | B_INPUT;  // OR_Gate or_1, 8 bits wide
  assign xor_1_out = A_INPUT ^ B_INPUT;  // XOR_Gate xor_1, 8 bits wide
  Shifter shifter_1 (.in(A_INPUT), .\dist (3'b001), .out(shifter_1_out));
  xor xor_2 (xor_2_out, A_INPUT[6], A_INPUT[7]);
  xor xor_3 (xor_3_out, C_IN, A_INPUT[7]);
  assign not_2_out = ~B_INPUT;  // NOT_Gate not_2, 8 bits wide
  Shifter #(.shift("lr")) shifter_2 (.in(A_INPUT), .\dist (3'b001), .out(shifter_2_out));
  Shifter shifter_3 (.in(A_INPUT), .\dist (3'b001), .out(shifter_3_out));
  Shifter #(.shift("ar")) shifter_4 (.in(A_INPUT), .\dist (3'b001), .out(shifter_4_out));
  Multiplexer #(.select(4), .width(8)) multiplexer_1 (
    .in0(A_INPUT), .in1(B_INPUT), .in2(not_1_out), .in3(not_2_out), .in4(adder_1_out),
    .in5(subtractor_1_out), .in6(subtractor_2_out), .in7(and_1_out), .in8(or_1_out), .in9(xor_1_out),
    .in10(shifter_1_out), .in11(shifter_2_out), .in12(shifter_3_out), .in13(shifter_4_out),
    .in14({A_INPUT[6:0], C_IN}), .in15({C_IN, A_INPUT[7:1]}), .out(OutALU), .sel(FunSel), .en(1'b1));
  nor nor_1 (OutFlag[3], OutALU[0], OutALU[1], OutALU[2], OutALU[3], OutALU[4], OutALU[5], OutALU[6], OutALU[7]);
  xnor xnor_1 (xnor_1_out, A_INPUT[7], B_INPUT[7]);
  xor xor_4 (xor_4_out, B_INPUT[7], OutALU[7]);
  xor xor_5 (xor_5_out, A_INPUT[7], B_INPUT[7]);
  xnor xnor_2 (xnor_2_out, OutALU[7], B_INPUT[7]);
  and and_2 (and_2_out, xnor_1_out, xor_4_out);
  and and_3 (and_3_out, xor_5_out, xnor_2_out);
  Multiplexer #(.select(4)) multiplexer_2 (
    .in0(1'b0), .in1(1'b0), .in2(1'b0), .in3(1'b0), .in4(adder_1_cout), .in5(subtractor_1_bout),
    .in6(subtractor_2_bout), .in7(1'b0), .in8(1'b0), .in9(1'b0), .in10(A_INPUT[7]), .in11(A_INPUT[0]),
    .in12(1'b0), .in13(1'b0), .in14(A_INPUT[7]), .in15(A_INPUT[0]), .out(OutFlag[2]), .sel(FunSel), .en(1'b1));
  Multiplexer #(.select(4)) multiplexer_3 (
    .in0(1'b0), .in1(1'b0), .in2(1'b0), .in3(1'b0), .in4(and_2_out), .in5(and_2_out), .in6(and_3_out),
    .in7(1'b0), .in8(1'b0), .in9(1'b0), .in10(1'b0), .in11(1'b0), .in12(xor_2_out), .in13(1'b0),
    .in14(xor_2_out), .in15(xor_3_out), .out(OutFlag[0]), .sel(FunSel), .en(1'b1));

  assign OutFlag[1] = OutALU[7];

  // Notes on the sheet:
  //   CSL
  //   CSR
  //   A+B Overflow
  //   A-B Overflow
endmodule

// ZCNO
module ZCNO_REG (
  input  [3:0] OutFlag,
  input  CLK,
  output C_OUT,
  output Z_OUT
);

  D_Flip_Flop O (.clk(CLK), .D(OutFlag[0]));  // open: Q, Qn, preset, en, reset
  D_Flip_Flop N (.clk(CLK), .D(OutFlag[1]));  // open: Q, Qn, preset, en, reset
  D_Flip_Flop C (.clk(CLK), .D(OutFlag[2]), .Q(C_OUT));  // open: Qn, preset, en, reset
  D_Flip_Flop Z (.clk(CLK), .D(OutFlag[3]), .Q(Z_OUT));  // open: Qn, preset, en, reset
endmodule
