// Logisim project Project3.circ as structural Verilog: 1 circuit, main circuit main
module main (
  output [15:0] IROut
);

  wire ALUFunSel0, ALUFunSel1, ALUFunSel2, ALUFunSel4, ALUFunSel5, ALUFunSel6, ALUFunSel7, ALUFunSel8,
       ALUFunSela, ALUFunSelb, and_1_out, and_2_out, and_3_out, and_4_out, and_5_out, and_6_out, and_7_out,
       and_8_out, and_11_out, and_12_out, and_13_out, and_14_out, and_15_out, and_16_out, and_17_out,
       and_18_out, and_19_out, and_20_out, and_21_out, and_25_out, and_26_out, and_27_out, and_28_out,
       and_29_out, and_30_out, and_31_out, and_32_out, and_33_out, and_34_out, and_35_out, and_36_out,
       and_37_out, and_38_out, and_39_out, and_40_out, and_41_out, and_42_out, and_43_out, and_44_out,
       and_45_out, and_46_out, and_47_out, and_48_out, and_49_out, and_50_out, and_51_out, and_52_out,
       and_53_out, and_54_out, and_55_out, and_56_out, and_57_out, and_59_out, and_60_out, and_62_out,
       and_63_out, and_64_out, and_65_out, and_66_out, and_67_out, and_68_out, and_69_out, and_70_out,
       and_71_out, and_72_out, and_73_out, and_75_out, and_76_out, and_77_out, and_78_out, and_79_out,
       and_80_out, and_81_out, and_82_out, and_83_out, and_84_out, and_85_out, and_86_out, and_87_out,
       and_88_out, and_89_out, and_90_out, and_91_out, and_92_out, and_93_out, and_94_out, and_95_out,
       and_96_out, and_97_out, and_98_out, and_99_out, and_100_out, and_101_out, and_102_out, and_103_out,
       and_104_out, AR__AR, AR__AR_GP, AR__GP, AR__GP_AR, AR__GP_GP, ARFunSel1, ARFunSel2, ARFunSel3,
       ARRegSel1, ARRegSel4, BO, CLK, CLR, E, GP__AR, GP__AR_GP, GP__GP, GP__GP_AR, GP__GP_GP, GPFunSel1,
       GPFunSel2, GPFunSel3, L_prime_H, MuxASel0, MuxASel1, MuxASel2, MuxASel3, MuxBSel1, MuxBSel2, MuxBSel3,
       MuxCSel, MuxCSel0, MuxCSel1, not_1_out, not_2_out, not_3_out, not_4_out, O0, O1, O2, O3, O4, O5, O6,
       O7, O8, O9, O10, O11, O12, O13, O14, O15, O16, O17, O18, or_1_out, or_2_out, or_3_out, or_4_out,
       or_5_out, or_6_out, or_7_out, or_8_out, or_9_out, or_10_out, or_11_out, or_12_out, or_13_out,
       or_14_out, or_15_out, or_16_out, or_17_out, or_18_out, or_19_out, or_20_out, or_21_out, or_22_out,
       or_23_out, or_24_out, or_25_out, or_26_out, or_27_out, or_28_out, or_29_out, or_30_out, or_31_out,
       or_32_out, or_33_out, or_34_out, or_35_out, or_36_out, or_37_out, or_38_out, or_39_out, or_40_out,
       or_41_out, or_42_out, or_46_out, or_47_out, or_48_out, or_49_out, or_50_out, or_51_out, or_52_out,
       or_53_out, or_54_out, or_55_out, or_60_out, or_61_out, or_62_out, or_67_out, or_68_out, or_69_out,
       or_70_out, or_75_out, or_76_out, or_78_out, or_81_out, or_82_out, or_83_out, or_86_out, or_88_out,
       or_89_out, or_91_out, or_92_out, or_95_out, or_96_out, or_99_out, or_100_out, or_101_out, or_102_out,
       or_103_out, or_104_out, OutDSel0, OutDSel1, OutDSel2, STR, T1, T2, T3, T4, T5, T6, T7, UO, Z;
  wire [1:0] ARFunSel, GPFunSel, multiplexer_2_out, multiplexer_3_out, multiplexer_4_out, MuxASel, MuxBSel,
       OutASel, OutBSel, OutCSel, OutDSel;
  wire [2:0] ARRegSel, counter_1_q, multiplexer_6_out;
  wire [3:0] ALUFunSel, GPRegSel, multiplexer_1_out, multiplexer_5_out;

  or or_1 (or_1_out, GP__GP, GP__AR);
  and and_1 (and_1_out, BO, T2, or_4_out);
  or or_2 (or_2_out, O7, O8);
  and and_2 (and_2_out, or_2_out, or_1_out, T4);
  or or_3 (or_3_out, AR__GP, AR__AR);
  or or_4 (or_4_out, GP__GP_GP, AR__GP_GP);
  buf or_5 (or_5_out, and_3_out);  // OR_Gate
  and and_3 (and_3_out, UO, T2, or_10_out);
  or or_6 (or_6_out, O7, O8);
  or or_7 (or_7_out, O2, O8, O7);
  or or_8 (or_8_out, AR__GP, AR__AR);
  and and_4 (and_4_out, UO, T2, or_3_out);
  assign OutASel = or_9_out ? IROut[3:2] : 2'bz;  // Controlled_Buffer controlled_buffer_1
  buf or_9 (or_9_out, and_1_out);  // OR_Gate
  assign OutASel = or_5_out ? IROut[6:5] : 2'bz;  // Controlled_Buffer controlled_buffer_2
  or or_10 (or_10_out, GP__GP, AR__GP);
  or or_11 (or_11_out, AR__AR, AR__GP);
  or or_12 (or_12_out, GP__GP, GP__AR);
  and and_5 (and_5_out, or_7_out, T2, or_8_out);
  and and_6 (and_6_out, BO, T2, or_13_out);
  or or_13 (or_13_out, AR__GP_GP, AR__AR_GP, AR__GP_AR);
  or or_14 (or_14_out, O2, O7, O8);
  or or_15 (or_15_out, GP__AR_GP, GP__GP_AR, AR__AR_GP, AR__GP_AR);
  or or_16 (or_16_out, GP__GP_GP, AR__GP_GP);
  or or_17 (or_17_out, GP__GP, AR__GP);
  or or_18 (or_18_out, O2, O7, O8);
  and and_7 (and_7_out, or_6_out, T4, or_11_out);
  or or_19 (or_19_out, O2, O7, O8);
  or or_20 (or_20_out, GP__GP, GP__AR, AR__GP);
  and and_8 (and_8_out, T2, O3);
  and and_9 (ALUFunSel2, O11, T2);
  or or_21 (or_21_out, GP__GP_AR, AR__GP_AR);
  or or_22 (or_22_out, GP__GP_GP, GP__AR_GP, AR__GP_GP, AR__AR_GP);
  and and_10 (ALUFunSelb, O13, T2);
  and and_11 (and_11_out, T3, O4);
  and and_12 (and_12_out, T2, BO, or_23_out);
  or or_23 (or_23_out, GP__GP_GP, GP__AR_GP, GP__GP_AR);
  Multiplexer #(.select(2), .width(4), .enable("false")) multiplexer_1 (
    .in0(4'b0001), .in1(4'b0010), .in2(4'b0100), .in3(4'b1000), .out(multiplexer_1_out), .sel(IROut[9:8]));
  Multiplexer #(.select(2), .width(2), .enable("false")) multiplexer_2 (
    .in0(2'b00), .in1(2'b00), .in2(2'b01), .in3(2'b10), .out(multiplexer_2_out), .sel(IROut[6:5]));
  or or_24 (or_24_out, GP__AR, AR__AR);
  Multiplexer #(.select(2), .width(2), .enable("false")) multiplexer_3 (
    .in0(2'b00), .in1(2'b00), .in2(2'b01), .in3(2'b10), .out(multiplexer_3_out), .sel(IROut[9:8]));
  and and_13 (and_13_out, or_14_out, T2, AR__AR);
  and and_14 (and_14_out, BO, T2, or_15_out);
  and and_15 (and_15_out, BO, T2, or_16_out);
  and and_16 (and_16_out, UO, T2, or_17_out);
  assign ALUFunSel = ALUFunSel0 ? 4'b0000 : 4'bz;  // Controlled_Buffer controlled_buffer_3
  assign ALUFunSel = ALUFunSel1 ? 4'b0001 : 4'bz;  // Controlled_Buffer controlled_buffer_4
  assign ALUFunSel = ALUFunSel2 ? 4'b0010 : 4'bz;  // Controlled_Buffer controlled_buffer_5
  assign ALUFunSel = ALUFunSel4 ? 4'b0100 : 4'bz;  // Controlled_Buffer controlled_buffer_6
  assign ALUFunSel = ALUFunSel5 ? 4'b0101 : 4'bz;  // Controlled_Buffer controlled_buffer_7
  assign ALUFunSel = ALUFunSel6 ? 4'b0110 : 4'bz;  // Controlled_Buffer controlled_buffer_8
  assign ALUFunSel = ALUFunSel7 ? 4'b0111 : 4'bz;  // Controlled_Buffer controlled_buffer_9
  assign ALUFunSel = ALUFunSel8 ? 4'b1000 : 4'bz;  // Controlled_Buffer controlled_buffer_10
  assign ALUFunSel = ALUFunSela ? 4'b1010 : 4'bz;  // Controlled_Buffer controlled_buffer_11
  assign ALUFunSel = ALUFunSelb ? 4'b1011 : 4'bz;  // Controlled_Buffer controlled_buffer_12
  and and_17 (and_17_out, O17, T2);
  and and_18 (and_18_out, or_19_out, T2, or_20_out);
  and and_19 (and_19_out, O5, T2);
  and and_20 (and_20_out, O6, or_21_out, T2);
  and and_21 (and_21_out, O6, or_22_out, T2);
  and and_22 (ALUFunSel7, O9, T2);
  and and_23 (ALUFunSel8, O10, T2);
  and and_24 (ALUFunSela, O12, T2);
  and and_25 (and_25_out, T2, O3);
  and and_26 (and_26_out, T3, O4);
  and and_27 (and_27_out, T2, O17);
  and and_28 (and_28_out, T3, O18);
  and and_29 (and_29_out, T2, O3);
  and and_30 (and_30_out, O17, T2);
  or or_25 (or_25_out, O2, O8, O7);
  and and_31 (and_31_out, or_25_out, T2, or_26_out);
  or or_26 (or_26_out, GP__GP, GP__AR);
  and and_32 (and_32_out, T2, UO, or_12_out);
  or or_27 (or_27_out, GP__GP, GP__AR);
  and and_33 (and_33_out, O1, T2);
  and and_34 (and_34_out, or_24_out, T2, UO);
  Multiplexer #(.select(2), .width(2), .enable("false")) multiplexer_4 (
    .in0(2'b00), .in1(2'b00), .in2(2'b01), .in3(2'b10), .out(multiplexer_4_out), .sel(IROut[3:2]));
  and and_35 (and_35_out, T4, or_28_out, or_29_out);
  or or_28 (or_28_out, O7, O8);
  or or_29 (or_29_out, GP__AR, AR__AR);
  not not_1 (not_1_out, Z);
  and and_36 (and_36_out, O17, T3);
  assign MuxCSel = MuxCSel0 ? 1'b0 : 1'bz;  // Controlled_Buffer controlled_buffer_13
  assign MuxCSel = MuxCSel1 ? 1'b1 : 1'bz;  // Controlled_Buffer controlled_buffer_14
  and and_37 (and_37_out, T2, or_18_out, AR__AR);
  and and_38 (and_38_out, T2, O1);
  Decoder #(.select(2), .enable("false")) decoder_1 (
    .out0(GP__GP), .out1(GP__AR), .out2(AR__GP), .out3(AR__AR), .sel({IROut[10], IROut[7]}));
  or or_30 (or_30_out, O7, O8, O2);
  or or_31 (or_31_out, AR__GP, AR__AR);
  or or_32 (or_32_out, AR__GP, AR__AR);
  and and_39 (and_39_out, T3, O4);
  or or_33 (or_33_out, O2, O8, O7);
  and and_40 (and_40_out, T2, BO, or_34_out);
  or or_34 (or_34_out, GP__GP_GP, GP__AR_GP, GP__GP_AR);
  or or_35 (or_35_out, GP__GP, GP__AR);
  and and_41 (and_41_out, O7, T3, or_27_out);
  Multiplexer #(.select(2), .width(4), .enable("false")) multiplexer_5 (
    .in0(4'b0001), .in1(4'b0010), .in2(4'b0100), .in3(4'b1000), .out(multiplexer_5_out), .sel(IROut[10:9]));
  and and_42 (and_42_out, UO, T2, or_36_out);
  or or_36 (or_36_out, GP__GP, GP__AR);
  and and_43 (and_43_out, O3, T2);
  assign OutBSel = or_37_out ? IROut[6:5] : 2'bz;  // Controlled_Buffer controlled_buffer_15
  or or_37 (or_37_out, and_64_out, and_85_out);
  buf or_38 (or_38_out, and_65_out);  // OR_Gate
  buf or_39 (or_39_out, and_94_out);  // OR_Gate
  assign OutCSel = or_40_out ? multiplexer_2_out : 2'bz;  // Controlled_Buffer controlled_buffer_16
  or or_40 (or_40_out, and_34_out, and_44_out, and_66_out);
  and and_44 (and_44_out, BO, T2, or_41_out);
  or or_41 (or_41_out, GP__GP_AR, AR__GP_AR);
  and and_45 (and_45_out, O14, T2);
  and and_46 (and_46_out, O15, T2, Z);
  and and_47 (and_47_out, O16, T2, not_1_out);
  or or_42 (or_42_out, O7, O8);
  or or_43 (ALUFunSel1, and_38_out, and_18_out, and_8_out, and_2_out);
  Clock clock_1 (.out(CLK));
  or or_44 (BO, O5, O6, O9, O10);
  or or_45 (UO, O11, O12, O13);
  or or_46 (or_46_out, AR__GP, AR__AR);
  and and_48 (and_48_out, T2, BO, or_47_out);
  or or_47 (or_47_out, AR__GP_GP, AR__AR_GP, AR__GP_AR);
  and and_49 (and_49_out, T2, UO, or_31_out);
  and and_50 (and_50_out, T2, O4);
  and and_51 (and_51_out, T3, or_32_out, O8);
  and and_52 (and_52_out, O18, T2);
  and and_53 (and_53_out, T2, O1);
  and and_54 (and_54_out, T2, O0, IROut[8]);
  and and_55 (and_55_out, T2, or_33_out, GP__AR);
  or or_48 (or_48_out, O2, O7, O8);
  and and_56 (and_56_out, or_48_out, T2, GP__GP);
  or or_49 (or_49_out, GP__GP, GP__AR);
  and and_57 (and_57_out, T2, O0);
  and and_58 (GPFunSel2, O8, T3, or_35_out);
  assign GPRegSel = and_59_out ? multiplexer_5_out : 4'bz;  // Controlled_Buffer controlled_buffer_17
  and and_59 (and_59_out, O0, T2);
  and and_60 (and_60_out, or_50_out, T2, GP__AR);
  or or_50 (or_50_out, O7, O8, O2);
  or or_51 (or_51_out, and_33_out, and_43_out);
  assign OutBSel = or_38_out ? IROut[3:2] : 2'bz;  // Controlled_Buffer controlled_buffer_18
  assign OutBSel = or_39_out ? IROut[9:8] : 2'bz;  // Controlled_Buffer controlled_buffer_19
  or or_52 (or_52_out, O8, O7, O2);
  assign OutCSel = or_53_out ? multiplexer_3_out : 2'bz;  // Controlled_Buffer controlled_buffer_20
  buf or_53 (or_53_out, and_35_out);  // OR_Gate
  assign MuxBSel = 1'b0 ? 2'b00 : 2'bz;  // Controlled_Buffer controlled_buffer_21
  assign MuxBSel = MuxBSel1 ? 2'b01 : 2'bz;  // Controlled_Buffer controlled_buffer_22
  assign MuxBSel = MuxBSel2 ? 2'b10 : 2'bz;  // Controlled_Buffer controlled_buffer_23
  assign MuxBSel = MuxBSel3 ? 2'b11 : 2'bz;  // Controlled_Buffer controlled_buffer_24
  and and_61 (MuxBSel2, O18, T3);
  or or_54 (or_54_out, AR__AR, AR__GP);
  or or_55 (or_55_out, GP__AR, AR__AR);
  or or_56 (ALUFunSel0, and_37_out, and_7_out, and_17_out);
  buf or_57 (ALUFunSel4, and_19_out);  // OR_Gate
  buf or_58 (ALUFunSel5, and_20_out);  // OR_Gate
  buf or_59 (ALUFunSel6, and_21_out);  // OR_Gate
  and and_62 (and_62_out, T2, or_30_out, or_46_out);
  or or_60 (or_60_out, AR__GP, AR__AR);
  assign MuxASel = MuxASel0 ? 2'b00 : 2'bz;  // Controlled_Buffer controlled_buffer_25
  assign MuxASel = MuxASel1 ? 2'b01 : 2'bz;  // Controlled_Buffer controlled_buffer_26
  assign MuxASel = MuxASel2 ? 2'b10 : 2'bz;  // Controlled_Buffer controlled_buffer_27
  assign MuxASel = MuxASel3 ? 2'b11 : 2'bz;  // Controlled_Buffer controlled_buffer_28
  not not_2 (not_2_out, IROut[8]);
  and and_63 (and_63_out, T2, UO, or_49_out);
  assign GPFunSel = 1'b0 ? 2'b00 : 2'bz;  // Controlled_Buffer controlled_buffer_29
  assign GPFunSel = GPFunSel1 ? 2'b01 : 2'bz;  // Controlled_Buffer controlled_buffer_30
  assign GPFunSel = GPFunSel2 ? 2'b10 : 2'bz;  // Controlled_Buffer controlled_buffer_31
  assign GPFunSel = GPFunSel3 ? 2'b11 : 2'bz;  // Controlled_Buffer controlled_buffer_32
  or or_61 (or_61_out, and_42_out, and_60_out, and_75_out, and_89_out, and_93_out, and_100_out);
  assign OutBSel = or_51_out ? IROut[10:9] : 2'bz;  // Controlled_Buffer controlled_buffer_33
  and and_64 (and_64_out, BO, T2, or_62_out);
  or or_62 (or_62_out, GP__GP_GP, GP__AR_GP, AR__GP_GP, AR__AR_GP);
  and and_65 (and_65_out, BO, T2, or_68_out);
  and and_66 (and_66_out, or_52_out, T2, or_69_out);
  and and_67 (and_67_out, BO, T2, or_70_out);
  and and_68 (and_68_out, or_42_out, T4, or_54_out);
  and and_69 (and_69_out, T2, UO, or_55_out);
  and and_70 (and_70_out, T2, O17);
  or or_63 (MuxCSel1, and_15_out, and_16_out);
  not not_3 (not_3_out, Z);
  and and_71 (and_71_out, T3, O17);
  and and_72 (and_72_out, T3, or_60_out, O7);
  and and_73 (and_73_out, T2, O1);
  or or_64 (STR, and_53_out, and_29_out, and_30_out);
  and and_74 (MuxASel0, T2, O0, not_2_out);
  or or_65 (GPFunSel1, and_57_out, and_31_out, and_11_out, and_12_out, and_32_out);
  buf or_66 (GPFunSel3, and_41_out);  // OR_Gate
  assign GPRegSel = or_61_out ? multiplexer_1_out : 4'bz;  // Controlled_Buffer controlled_buffer_34
  and and_75 (and_75_out, or_67_out, T3, or_75_out);
  or or_67 (or_67_out, O7, O8);
  or or_68 (or_68_out, GP__GP_AR, AR__GP_AR);
  or or_69 (or_69_out, GP__AR, AR__AR);
  assign OutCSel = and_67_out ? multiplexer_4_out : 2'bz;  // Controlled_Buffer controlled_buffer_35
  or or_70 (or_70_out, GP__AR_GP, AR__AR_GP);
  or or_71 (MuxBSel1, and_45_out, and_46_out, and_47_out, and_36_out);
  Multiplexer #(.select(2), .width(3), .enable("false")) multiplexer_6 (
    .in0(3'b001), .in1(3'b001), .in2(3'b010), .in3(3'b100), .out(multiplexer_6_out), .sel(IROut[9:8]));
  and and_76 (and_76_out, T2, UO, or_78_out);
  and and_77 (and_77_out, O3, T2);
  and and_78 (and_78_out, O4, T2);
  and and_79 (and_79_out, O17, T2);
  and and_80 (and_80_out, O18, T2);
  and and_81 (and_81_out, T2, O14);
  and and_82 (and_82_out, T2, O15, Z);
  and and_83 (and_83_out, T2, O16, not_3_out);
  assign OutDSel = OutDSel0 ? 2'b00 : 2'bz;  // Controlled_Buffer controlled_buffer_36
  assign OutDSel = OutDSel1 ? 2'b01 : 2'bz;  // Controlled_Buffer controlled_buffer_37
  assign OutDSel = OutDSel2 ? 2'b10 : 2'bz;  // Controlled_Buffer controlled_buffer_38
  assign OutDSel = 1'b0 ? 2'b11 : 2'bz;  // Controlled_Buffer controlled_buffer_39
  and and_84 (and_84_out, T2, O0, IROut[8]);
  or or_72 (MuxASel1, and_54_out, and_39_out);
  buf or_73 (MuxASel2, and_55_out);  // OR_Gate
  or or_74 (MuxASel3, and_56_out, and_40_out, and_63_out);
  or or_75 (or_75_out, GP__GP, GP__AR);
  and and_85 (and_85_out, or_76_out, T2, or_82_out);
  or or_76 (or_76_out, O7, O2, O8);
  assign OutCSel = or_83_out ? 2'b00 : 2'bz;  // Controlled_Buffer controlled_buffer_40
  or or_77 (MuxBSel3, and_5_out, and_6_out, and_4_out);
  Counter #(.width(3), .max('h7)) counter_1 (.Q(counter_1_q), .clk(CLK), .clr(CLR));  // open: load, D, count, carry
  Decoder #(.select(5), .enable("false")) decoder_2 (
    .out0(O0), .out1(O1), .out2(O2), .out3(O3), .out4(O4), .out5(O5), .out6(O6), .out7(O7), .out8(O8),
    .out9(O9), .out10(O10), .out11(O11), .out12(O12), .out13(O13), .out14(O14), .out15(O15), .out16(O16),
    .out17(O17), .out18(O18), .sel(IROut[15:11]));  // open: out19, out20, out21, out22, out23, out24, out25, out26, out27, out28, out29, out30, out31
  assign ARRegSel = 1'b0 ? 3'b000 : 3'bz;  // Controlled_Buffer controlled_buffer_41
  assign ARRegSel = ARRegSel1 ? 3'b001 : 3'bz;  // Controlled_Buffer controlled_buffer_42
  assign ARRegSel = 1'b0 ? 3'b010 : 3'bz;  // Controlled_Buffer controlled_buffer_43
  assign ARRegSel = ARRegSel4 ? 3'b100 : 3'bz;  // Controlled_Buffer controlled_buffer_44
  or or_78 (or_78_out, AR__GP, AR__AR);
  and and_86 (and_86_out, T3, O18);
  and and_87 (and_87_out, O3, T2);
  and and_88 (and_88_out, O17, T2);
  or or_79 (OutDSel0, L_prime_H, T1);
  or or_80 (OutDSel1, and_84_out, and_73_out);
  and and_89 (and_89_out, BO, T2, or_81_out);
  or or_81 (or_81_out, GP__GP_GP, GP__AR_GP, GP__GP_AR);
  or or_82 (or_82_out, GP__GP, AR__GP);
  and and_90 (and_90_out, T2, O17);
  buf or_83 (or_83_out, and_90_out);  // OR_Gate
  or or_84 (MuxCSel0, and_13_out, and_14_out, and_68_out, and_69_out, and_70_out);
  Decoder #(.select(3), .enable("false")) decoder_3 (
    .out0(L_prime_H), .out1(T1), .out2(T2), .out3(T3), .out4(T4), .out5(T5), .out6(T6), .out7(T7),
    .sel(counter_1_q));
  or or_85 (E, L_prime_H, T1);
  or or_86 (or_86_out, AR__GP, AR__AR);
  and and_91 (and_91_out, T3, O18);
  and and_92 (and_92_out, T2, O16, not_4_out);
  not not_4 (not_4_out, Z);
  or or_87 (OutDSel2, and_25_out, and_26_out, and_27_out, and_28_out);
  and and_93 (and_93_out, O4, T3);
  and and_94 (and_94_out, T4, or_88_out, or_91_out);
  or or_88 (or_88_out, O7, O8);
  and and_95 (and_95_out, or_86_out, T3, or_89_out);
  or or_89 (or_89_out, O8, O7);
  and and_96 (and_96_out, T2, O14);
  and and_97 (and_97_out, T2, O15, Z);
  and and_98 (and_98_out, T3, O17);
  assign ARFunSel = 1'b0 ? 2'b00 : 2'bz;  // Controlled_Buffer controlled_buffer_45
  assign ARFunSel = ARFunSel1 ? 2'b01 : 2'bz;  // Controlled_Buffer controlled_buffer_46
  assign ARFunSel = ARFunSel2 ? 2'b10 : 2'bz;  // Controlled_Buffer controlled_buffer_47
  assign ARFunSel = ARFunSel3 ? 2'b11 : 2'bz;  // Controlled_Buffer controlled_buffer_48
  or or_90 (ARFunSel3, and_87_out, and_72_out, and_88_out);
  or or_91 (or_91_out, GP__GP, GP__AR);
  part2 part2_1 (
    .GPRegSel(GPRegSel), .GPFunSel(GPFunSel), .OutBSel(OutBSel), .OutASel(OutASel), .MuxASel(MuxASel),
    .ARRegSel(ARRegSel), .ARFunSel(ARFunSel), .L_prime__H(L_prime_H), .E(E), .IRFunSel(2'b11),
    .OutDSel(OutDSel), .OutCSel(OutCSel), .MuxBSel(MuxBSel), .IROut(IROut), .MuxCSel(MuxCSel),
    .ALUFunSel(ALUFunSel), .CLK(CLK), .STR(STR), .Z(Z));
  assign ARRegSel = or_92_out ? multiplexer_6_out : 3'bz;  // Controlled_Buffer controlled_buffer_49
  or or_92 (or_92_out, and_76_out, and_95_out, and_99_out, and_101_out);
  or or_93 (ARRegSel1, and_91_out, L_prime_H, T1, and_96_out, and_97_out, and_92_out, and_98_out);
  or or_94 (ARFunSel1, and_62_out, and_48_out, and_49_out, and_81_out, and_82_out, and_83_out, and_71_out, and_86_out);
  or or_95 (or_95_out, O14, O15);
  and and_99 (and_99_out, T2, BO, or_96_out);
  or or_96 (or_96_out, AR__GP_GP, AR__AR_GP, AR__GP_AR);
  or or_97 (ARRegSel4, and_77_out, and_78_out, and_79_out, and_80_out);
  or or_98 (ARFunSel2, L_prime_H, T1, and_50_out, and_51_out, and_52_out);
  and and_100 (and_100_out, or_99_out, T2, GP__GP);
  or or_99 (or_99_out, O7, O8, O2);
  or or_100 (or_100_out, O8, O7);
  and and_101 (and_101_out, T2, or_101_out, or_103_out);
  or or_101 (or_101_out, O7, O8, O2);
  or or_102 (or_102_out, O4, O17, O18);
  and and_102 (and_102_out, or_100_out, T5);
  or or_103 (or_103_out, AR__GP, AR__AR);
  or or_104 (or_104_out, O0, O1, O2, O3, BO, UO, or_95_out);
  and and_103 (and_103_out, or_102_out, T4);
  Decoder #(.select(3), .enable("false")) decoder_4 (
    .out0(GP__GP_GP), .out1(GP__AR_GP), .out2(GP__GP_AR), .out4(AR__GP_GP), .out5(AR__AR_GP),
    .out6(AR__GP_AR), .sel({IROut[10], IROut[7], IROut[4]}));  // open: out3, out7
  and and_104 (and_104_out, or_104_out, T3);
  or or_105 (CLR, and_104_out, and_103_out, and_102_out);

  // Other names for the same wires on the sheet: I4 = IROut[4]; I7 = IROut[7]; I10 = IROut[10]; I0 = IROut[0];
  //   I1 = IROut[1]; I2 = IROut[2]; I3 = IROut[3]; I5 = IROut[5]; I6 = IROut[6]; I8 = IROut[8]; I9 = IROut[9];
  //   I11 = IROut[11]; I12 = IROut[12]; I13 = IROut[13]; I14 = IROut[14]; I15 = IROut[15]; T0 = L_prime_H

  // Notes on the sheet:
  //   ALUFunSel
  //   ALUFunSel1
  //   ALUFunSel2
  //   ALUFunSel4
  //   ALUFunSel5
  //   ALUFunSel6
  //   ALUFunSel7
  //   ALUFunSel8
  //   ALUFunSela
  //   ALUFunSelb
  //   MuxCSel
  //   MuxCSel0
  //   MuxCSel1
  //   ALUFunSel0
  //   OutASel
  //   GPFunSel
  //   GPFunSel0
  //   GPFunSel1
  //   GPFunSel2
  //   GPFunSel3
  //   GPRegSel
  //   MuxBSel
  //   MuxBSel0
  //   MuxBSel1
  //   MuxBSel3
  //   MuxASel
  //   MuxASel0
  //   MuxASel1
  //   MuxASel2
  //   MuxASel3
  //   OutBSel
  //   OutCSel
  //   MuxBSel2
  //   TIMING SIGNALS
  //   OutDSel
  //   OutDSel0
  //   OutDSel1
  //   OutDSel2
  //   OutDSel3
  //   STR
  //   DECODE
  //   Enable
  //   IRFunSel
  //   ARRegSel
  //   ARFunSel3
  //   L'/H
  //   ARRegSel0
  //   ARRegSel1
  //   ARRegSel2
  //   ARRegSel4
  //   ARFunSel
  //   ARFunSel0
  //   ARFunSel1
  //   ARFunSel2
  //   RESET
  //   SRC2
  //   DST
  //   SRC1
endmodule
