// Logisim project project4.circ as structural Verilog: 1 circuit, main circuit main
module main (
  output [15:0] IROut
);

  wire ADD, ALUFunSel0, ALUFunSel1, ALUFunSel2, ALUFunSel4, ALUFunSel5, ALUFunSel6, ALUFunSel7, ALUFunSel8,
       ALUFunSela, ALUFunSelb, and_2_out, and_3_out, and_4_out, and_5_out, and_7_out, and_8_out, and_9_out,
       and_10_out, and_11_out, and_12_out, and_14_out, and_15_out, and_16_out, and_17_out, and_18_out,
       and_19_out, and_20_out, and_21_out, and_22_out, and_23_out, and_24_out, and_25_out, and_26_out,
       and_28_out, and_29_out, and_30_out, and_31_out, and_32_out, and_33_out, and_34_out, and_35_out,
       and_36_out, and_37_out, and_38_out, and_39_out, and_40_out, and_41_out, and_42_out, and_43_out,
       and_44_out, and_45_out, and_46_out, and_47_out, and_49_out, and_50_out, and_51_out, and_52_out,
       and_53_out, and_54_out, and_55_out, and_56_out, and_57_out, and_58_out, and_59_out, and_60_out,
       and_61_out, and_62_out, and_63_out, and_65_out, and_66_out, and_67_out, and_68_out, and_69_out,
       and_71_out, and_72_out, and_74_out, and_75_out, and_76_out, and_77_out, and_78_out, and_79_out,
       and_80_out, and_81_out, and_82_out, and_83_out, and_84_out, and_85_out, and_86_out, and_87_out,
       and_88_out, and_89_out, and_90_out, and_91_out, and_92_out, AR__AR, AR__AR_GP, AR__GP, AR__GP_AR,
       AR__GP_GP, ARFunSel1, ARFunSel2, ARFunSel3, ARRegSel1, ARRegSel4, BNE, BO, BRANCH, C, CALL, CD_TYPE,
       CLK, DEC, E, F0, FETCH, FETCH0, GP__AR, GP__AR_GP, GP__GP, GP__GP_AR, GP__GP_GP, GPFunSel1, GPFunSel2,
       GPFunSel3, INC, JMP, L_prime_H, LOAD, MAP, MOVE, multiplexer_6_out, multiplexer_10_out, MuxASel0,
       MuxASel1, MuxASel2, MuxASel3, MuxBSel1, MuxBSel2, MuxBSel3, MuxCSel, MuxCSel0, MuxCSel1, NOP0, NOP1,
       nor_1_out, not_1_out, not_2_out, not_3_out, not_4_out, not_5_out, not_6_out, not_7_out, not_9_out,
       or_1_out, or_2_out, or_3_out, or_4_out, or_5_out, or_6_out, or_7_out, or_8_out, or_9_out, or_10_out,
       or_11_out, or_14_out, or_15_out, or_16_out, or_17_out, or_18_out, or_19_out, or_20_out, or_21_out,
       or_22_out, or_23_out, or_24_out, or_25_out, or_26_out, or_27_out, or_28_out, or_29_out, or_30_out,
       or_31_out, or_32_out, or_33_out, or_36_out, or_37_out, or_38_out, or_39_out, or_40_out, or_41_out,
       or_42_out, or_43_out, or_44_out, or_45_out, or_46_out, or_47_out, or_48_out, or_49_out, or_50_out,
       or_51_out, or_52_out, or_53_out, or_54_out, or_58_out, or_59_out, or_62_out, or_71_out, or_72_out,
       or_73_out, or_75_out, or_76_out, or_77_out, or_78_out, or_81_out, or_82_out, or_85_out, or_86_out,
       or_89_out, or_90_out, OutDSel1, OutDSel2, PULL, PUSH, RET, SBRE, STORE, STR, SUB, UO, Z;
  wire [1:0] ARFunSel, BR, BR_TYPE, counter_1_q, GPFunSel, multiplexer_1_out, multiplexer_7_out,
       multiplexer_8_out, MuxASel, MuxBSel, OutASel, OutBSel, OutCSel, OutDSel;
  wire [2:0] ARRegSel, multiplexer_5_out;
  wire [3:0] ALUFunSel, F1, GPRegSel, multiplexer_2_out, multiplexer_3_out;
  wire [7:0] AD, adder_1_out, CAR_q, multiplexer_4_out, SBR_q;

  Clock u_CLK (.out(CLK));
  Decoder #(.select(2), .enable("false")) decoder_1 (.out0(JMP), .out1(CALL), .out2(RET), .out3(MAP), .sel(BR_TYPE));
  and and_1 (SBRE, C, CALL);
  Decoder #(.select(2), .enable("false")) decoder_2 (
    .out0(GP__GP), .out1(GP__AR), .out2(AR__GP), .out3(AR__AR), .sel({IROut[10], IROut[7]}));
  not not_1 (not_1_out, IROut[15]);
  and and_2 (and_2_out, BO, or_1_out);
  or or_1 (or_1_out, GP__GP_GP, GP__AR_GP, AR__GP_GP, AR__AR_GP);
  nor nor_1 (nor_1_out, IROut[11], IROut[12], IROut[13], IROut[14], not_1_out);
  or or_2 (or_2_out, ADD, SUB, ALUFunSel7, ALUFunSel8);
  or or_3 (or_3_out, GP__GP_GP, GP__AR_GP, GP__GP_AR);
  or or_4 (or_4_out, GP__GP, GP__AR);
  or or_5 (or_5_out, MOVE, DEC, INC);
  and and_3 (and_3_out, UO, or_6_out);
  or or_6 (or_6_out, AR__GP, AR__AR);
  and and_4 (and_4_out, BO, or_11_out);
  and and_5 (and_5_out, MOVE, FETCH);
  or or_7 (or_7_out, GP__GP, GP__AR);
  and and_6 (BNE, nor_1_out, not_2_out);
  not not_2 (not_2_out, FETCH0);
  Multiplexer #(.select(2), .width(2), .enable("false")) multiplexer_1 (
    .in0(2'b00), .in1(2'b00), .in2(2'b01), .in3(2'b10), .out(multiplexer_1_out), .sel(IROut[3:2]));
  or or_8 (or_8_out, GP__GP, GP__AR);
  and and_7 (and_7_out, NOP0, PULL);
  and and_8 (and_8_out, BO, or_3_out);
  and and_9 (and_9_out, UO, or_4_out);
  Multiplexer #(.select(2), .width(4), .enable("false")) multiplexer_2 (
    .in0(4'b0001), .in1(4'b0010), .in2(4'b0100), .in3(4'b1000), .out(multiplexer_2_out), .sel(IROut[9:8]));
  and and_10 (and_10_out, or_5_out, or_9_out);
  or or_9 (or_9_out, AR__GP, AR__AR);
  and and_11 (and_11_out, BO, or_10_out);
  or or_10 (or_10_out, AR__GP_GP, AR__AR_GP, AR__GP_AR);
  or or_11 (or_11_out, GP__GP_GP, AR__GP_GP);
  and and_12 (and_12_out, and_5_out, or_7_out);
  or or_12 (UO, ALUFunSel2, ALUFunSela, ALUFunSelb);
  or or_13 (BO, ADD, SUB, ALUFunSel7, ALUFunSel8);
  and and_13 (FETCH0, FETCH, NOP1);
  not not_3 (not_3_out, C);
  assign OutCSel = and_14_out ? multiplexer_1_out : 2'bz;  // Controlled_Buffer controlled_buffer_1
  and and_14 (and_14_out, or_2_out, IROut[4]);
  or or_14 (or_14_out, AR__GP, AR__AR);
  or or_15 (or_15_out, AR__GP, AR__AR);
  and and_15 (and_15_out, MOVE, or_8_out);
  and and_16 (and_16_out, INC, NOP0);
  or or_16 (or_16_out, GP__GP, GP__AR);
  or or_17 (or_17_out, GP__GP, GP__AR);
  Multiplexer #(.select(2), .width(4), .enable("false")) multiplexer_3 (
    .in0(4'b0001), .in1(4'b0010), .in2(4'b0100), .in3(4'b1000), .out(multiplexer_3_out), .sel(IROut[10:9]));
  and and_17 (and_17_out, UO, or_18_out);
  or or_18 (or_18_out, GP__GP, GP__AR);
  and and_18 (and_18_out, NOP0, PUSH);
  assign OutASel = or_19_out ? IROut[6:5] : 2'bz;  // Controlled_Buffer controlled_buffer_2
  buf or_19 (or_19_out, and_19_out);  // OR_Gate
  and and_19 (and_19_out, UO, or_30_out);
  and and_20 (and_20_out, FETCH, MOVE);
  or or_20 (or_20_out, AR__AR, AR__GP);
  part2 part2_1 (
    .GPRegSel(GPRegSel), .GPFunSel(GPFunSel), .OutBSel(OutBSel), .OutASel(OutASel), .MuxASel(MuxASel),
    .ARRegSel(ARRegSel), .ARFunSel(ARFunSel), .L_prime__H(L_prime_H), .E(E), .IRFunSel(2'b11),
    .OutDSel(OutDSel), .OutCSel(OutCSel), .MuxBSel(MuxBSel), .IROut(IROut), .MuxCSel(MuxCSel),
    .ALUFunSel(ALUFunSel), .CLK(CLK), .STR(STR), .Z(Z));
  Multiplexer #(.select(2), .width(8), .enable("false")) multiplexer_4 (
    .in0(adder_1_out), .in1(AD), .in2(SBR_q), .in3({1'b1, IROut[15:11], 2'b00}), .out(multiplexer_4_out),
    .sel(BR));
  and and_21 (and_21_out, not_3_out, or_21_out);
  or or_21 (or_21_out, JMP, CALL);
  and and_22 (and_22_out, LOAD, IROut[8]);
  and and_23 (and_23_out, STORE, NOP0);
  or or_22 (or_22_out, AR__GP, AR__AR);
  or or_23 (or_23_out, AR__GP_GP, AR__AR_GP, AR__GP_AR);
  and and_24 (and_24_out, UO, or_14_out);
  Multiplexer #(.select(2), .width(3), .enable("false")) multiplexer_5 (
    .in0(3'b001), .in1(3'b001), .in2(3'b010), .in3(3'b100), .out(multiplexer_5_out), .sel(IROut[9:8]));
  and and_25 (and_25_out, UO, or_36_out);
  and and_26 (and_26_out, FETCH, INC);
  or or_24 (or_24_out, MOVE, DEC, INC);
  or or_25 (or_25_out, GP__GP_GP, GP__AR_GP, GP__GP_AR);
  and and_27 (GPFunSel2, and_16_out, or_16_out);
  and and_28 (and_28_out, DEC, or_17_out);
  assign GPRegSel = and_29_out ? multiplexer_3_out : 4'bz;  // Controlled_Buffer controlled_buffer_3
  and and_29 (and_29_out, LOAD, NOP0);
  assign OutBSel = or_26_out ? IROut[6:5] : 2'bz;  // Controlled_Buffer controlled_buffer_4
  or or_26 (or_26_out, and_2_out, and_41_out);
  assign OutBSel = or_27_out ? IROut[3:2] : 2'bz;  // Controlled_Buffer controlled_buffer_5
  buf or_27 (or_27_out, and_56_out);  // OR_Gate
  assign OutBSel = or_28_out ? IROut[9:8] : 2'bz;  // Controlled_Buffer controlled_buffer_6
  buf or_28 (or_28_out, and_87_out);  // OR_Gate
  not not_4 (not_4_out, C);
  assign OutASel = or_29_out ? IROut[3:2] : 2'bz;  // Controlled_Buffer controlled_buffer_7
  buf or_29 (or_29_out, and_4_out);  // OR_Gate
  or or_30 (or_30_out, GP__GP, AR__GP);
  and and_30 (and_30_out, and_20_out, or_20_out);
  or or_31 (or_31_out, MOVE, DEC, INC);
  or or_32 (or_32_out, GP__GP, GP__AR, AR__GP);
  and and_31 (and_31_out, FETCH0, CLK);
  assign BR = multiplexer_6_out ? 2'b00 : 2'bz;  // Controlled_Buffer controlled_buffer_8
  Multiplexer #(.enable("false")) multiplexer_6 (
    .in0(and_21_out), .in1(and_47_out), .out(multiplexer_6_out), .sel(BNE));
  Multiplexer #(.select(2), .width(2), .enable("false")) multiplexer_7 (
    .in0(2'b00), .in1(2'b00), .in2(2'b01), .in3(2'b10), .out(multiplexer_7_out), .sel(IROut[6:5]));
  or or_33 (or_33_out, ADD, SUB, ALUFunSel7, ALUFunSel8, INC, DEC, MOVE, ALUFunSel2, ALUFunSela, ALUFunSelb);
  assign OutDSel = FETCH0 ? 2'b00 : 2'bz;  // Controlled_Buffer controlled_buffer_9
  assign OutDSel = OutDSel1 ? 2'b01 : 2'bz;  // Controlled_Buffer controlled_buffer_10
  assign OutDSel = OutDSel2 ? 2'b10 : 2'bz;  // Controlled_Buffer controlled_buffer_11
  or or_34 (OutDSel1, and_22_out, and_23_out);
  or or_35 (OutDSel2, PUSH, PULL);
  and and_32 (and_32_out, MOVE, or_22_out);
  and and_33 (and_33_out, BO, or_23_out);
  and and_34 (and_34_out, FETCH, INC);
  and and_35 (and_35_out, or_15_out, INC);
  assign ARRegSel = 1'b0 ? 3'b000 : 3'bz;  // Controlled_Buffer controlled_buffer_12
  assign ARRegSel = ARRegSel1 ? 3'b001 : 3'bz;  // Controlled_Buffer controlled_buffer_13
  assign ARRegSel = 1'b0 ? 3'b010 : 3'bz;  // Controlled_Buffer controlled_buffer_14
  assign ARRegSel = ARRegSel4 ? 3'b100 : 3'bz;  // Controlled_Buffer controlled_buffer_15
  or or_36 (or_36_out, AR__GP, AR__AR);
  and and_36 (and_36_out, PULL, FETCH);
  and and_37 (and_37_out, NOP0, PULL);
  or or_37 (or_37_out, MOVE, DEC, INC);
  and and_38 (and_38_out, BO, or_25_out);
  or or_38 (or_38_out, GP__GP, GP__AR);
  assign GPFunSel = 1'b0 ? 2'b00 : 2'bz;  // Controlled_Buffer controlled_buffer_16
  assign GPFunSel = GPFunSel1 ? 2'b01 : 2'bz;  // Controlled_Buffer controlled_buffer_17
  assign GPFunSel = GPFunSel2 ? 2'b10 : 2'bz;  // Controlled_Buffer controlled_buffer_18
  assign GPFunSel = GPFunSel3 ? 2'b11 : 2'bz;  // Controlled_Buffer controlled_buffer_19
  and and_39 (and_39_out, LOAD, NOP0);
  and and_40 (and_40_out, or_39_out, GP__AR);
  or or_39 (or_39_out, MOVE, DEC, INC);
  assign OutBSel = or_40_out ? IROut[10:9] : 2'bz;  // Controlled_Buffer controlled_buffer_20
  or or_40 (or_40_out, and_18_out, STORE);
  and and_41 (and_41_out, or_51_out, or_76_out);
  and and_42 (and_42_out, BRANCH, C);
  and and_43 (and_43_out, BRANCH, not_4_out);
  or or_41 (or_41_out, MOVE, DEC, INC);
  or or_42 (or_42_out, GP__AR_GP, GP__GP_AR, AR__AR_GP, AR__GP_AR);
  or or_43 (or_43_out, GP__GP_GP, AR__GP_GP);
  or or_44 (or_44_out, GP__GP, AR__GP);
  assign ALUFunSel = ALUFunSel0 ? 4'b0000 : 4'bz;  // Controlled_Buffer controlled_buffer_21
  assign ALUFunSel = ALUFunSel1 ? 4'b0001 : 4'bz;  // Controlled_Buffer controlled_buffer_22
  assign ALUFunSel = ALUFunSel2 ? 4'b0010 : 4'bz;  // Controlled_Buffer controlled_buffer_23
  assign ALUFunSel = ALUFunSel4 ? 4'b0100 : 4'bz;  // Controlled_Buffer controlled_buffer_24
  assign ALUFunSel = ALUFunSel5 ? 4'b0101 : 4'bz;  // Controlled_Buffer controlled_buffer_25
  assign ALUFunSel = ALUFunSel6 ? 4'b0110 : 4'bz;  // Controlled_Buffer controlled_buffer_26
  assign ALUFunSel = ALUFunSel7 ? 4'b0111 : 4'bz;  // Controlled_Buffer controlled_buffer_27
  assign ALUFunSel = ALUFunSel8 ? 4'b1000 : 4'bz;  // Controlled_Buffer controlled_buffer_28
  assign ALUFunSel = ALUFunSela ? 4'b1010 : 4'bz;  // Controlled_Buffer controlled_buffer_29
  assign ALUFunSel = ALUFunSelb ? 4'b1011 : 4'bz;  // Controlled_Buffer controlled_buffer_30
  and and_44 (and_44_out, or_31_out, NOP0);
  and and_45 (and_45_out, and_44_out, or_32_out);
  and and_46 (and_46_out, NOP0, PUSH);
  or or_45 (or_45_out, GP__GP_AR, AR__GP_AR);
  or or_46 (or_46_out, GP__GP_GP, GP__AR_GP, AR__GP_GP, AR__AR_GP);
  Counter #(.width(2), .max('h2)) counter_1 (.Q(counter_1_q), .clk(and_31_out));  // open: load, D, count, carry, clr
  Decoder #(.enable("false")) decoder_3 (.out0(NOP0), .out1(FETCH), .sel(F0));
  and and_47 (and_47_out, Z, CALL);
  and and_48 (E, FETCH0, NOP1);
  assign OutCSel = and_49_out ? multiplexer_7_out : 2'bz;  // Controlled_Buffer controlled_buffer_31
  and and_49 (and_49_out, or_33_out, IROut[7]);
  assign ARFunSel = ARFunSel1 ? 2'b01 : 2'bz;  // Controlled_Buffer controlled_buffer_32
  assign ARFunSel = ARFunSel2 ? 2'b10 : 2'bz;  // Controlled_Buffer controlled_buffer_33
  assign ARFunSel = ARFunSel3 ? 2'b11 : 2'bz;  // Controlled_Buffer controlled_buffer_34
  not not_5 (not_5_out, C);
  and and_50 (and_50_out, FETCH, PUSH);
  or or_47 (or_47_out, AR__GP, AR__AR);
  or or_48 (or_48_out, AR__GP, AR__AR);
  and and_51 (and_51_out, BRANCH, not_6_out);
  not not_6 (not_6_out, C);
  assign MuxASel = MuxASel0 ? 2'b00 : 2'bz;  // Controlled_Buffer controlled_buffer_35
  assign MuxASel = MuxASel1 ? 2'b01 : 2'bz;  // Controlled_Buffer controlled_buffer_36
  assign MuxASel = MuxASel2 ? 2'b10 : 2'bz;  // Controlled_Buffer controlled_buffer_37
  assign MuxASel = MuxASel3 ? 2'b11 : 2'bz;  // Controlled_Buffer controlled_buffer_38
  not not_7 (not_7_out, IROut[8]);
  and and_52 (and_52_out, LOAD, IROut[8]);
  and and_53 (and_53_out, NOP0, or_24_out, GP__AR);
  and and_54 (and_54_out, or_37_out, GP__GP);
  and and_55 (and_55_out, UO, or_38_out);
  assign GPRegSel = or_49_out ? multiplexer_2_out : 4'bz;  // Controlled_Buffer controlled_buffer_39
  or or_49 (or_49_out, and_17_out, and_40_out, and_71_out, and_75_out, and_82_out, and_91_out);
  or or_50 (or_50_out, DEC, INC);
  buf or_51 (or_51_out, and_72_out);  // OR_Gate
  and and_56 (and_56_out, BO, or_52_out);
  or or_52 (or_52_out, GP__GP_AR, AR__GP_AR);
  assign MuxBSel = 1'b0 ? 2'b00 : 2'bz;  // Controlled_Buffer controlled_buffer_40
  assign MuxBSel = MuxBSel1 ? 2'b01 : 2'bz;  // Controlled_Buffer controlled_buffer_41
  assign MuxBSel = MuxBSel2 ? 2'b10 : 2'bz;  // Controlled_Buffer controlled_buffer_42
  assign MuxBSel = MuxBSel3 ? 2'b11 : 2'bz;  // Controlled_Buffer controlled_buffer_43
  and and_57 (and_57_out, or_41_out, AR__AR);
  and and_58 (and_58_out, BO, or_42_out);
  and and_59 (and_59_out, BO, or_43_out);
  and and_60 (and_60_out, UO, or_44_out);
  or or_53 (or_53_out, MOVE, DEC, INC);
  and and_61 (and_61_out, or_53_out, AR__AR);
  and and_62 (and_62_out, SUB, or_45_out);
  and and_63 (and_63_out, SUB, or_46_out);
  _8_bit_register CAR (.CLK(CLK), .FunSel(2'b01), .E(1'b1), .I(multiplexer_4_out), .Q(CAR_q));
  not not_8 (L_prime_H, counter_1_q[0]);
  and and_64 (BRANCH, FETCH, LOAD);
  and and_65 (and_65_out, BRANCH, C);
  and and_66 (and_66_out, BRANCH, not_5_out);
  and and_67 (and_67_out, or_47_out, DEC);
  and and_68 (and_68_out, or_48_out, or_54_out);
  or or_54 (or_54_out, DEC, INC);
  and and_69 (and_69_out, BRANCH, C);
  or or_55 (STR, STORE, PUSH);
  and and_70 (MuxASel0, LOAD, not_7_out);
  or or_56 (GPFunSel1, and_39_out, and_15_out, and_7_out, and_8_out, and_9_out);
  buf or_57 (GPFunSel3, and_28_out);  // OR_Gate
  and and_71 (and_71_out, or_50_out, or_58_out);
  or or_58 (or_58_out, GP__GP, GP__AR);
  and and_72 (and_72_out, or_59_out, NOP0);
  or or_59 (or_59_out, DEC, MOVE, INC);
  and and_73 (MuxBSel2, FETCH, PULL);
  assign MuxCSel = MuxCSel0 ? 1'b0 : 1'bz;  // Controlled_Buffer controlled_buffer_44
  assign MuxCSel = MuxCSel1 ? 1'b1 : 1'bz;  // Controlled_Buffer controlled_buffer_45
  Adder adder_1 (.a(8'h1), .b(CAR_q), .out(adder_1_out));  // open: cin, cout
  Decoder #(.select(4), .enable("false")) decoder_4 (
    .out0(NOP1), .out1(ADD), .out2(SUB), .out3(ALUFunSel7), .out4(ALUFunSel8), .out5(ALUFunSel2),
    .out6(ALUFunSela), .out7(ALUFunSelb), .out8(LOAD), .out9(STORE), .out10(MOVE), .out11(INC), .out12(DEC),
    .out13(PUSH), .out14(PULL), .sel(F1));  // open: out15
  not not_9 (not_9_out, Z);
  Multiplexer #(.select(2), .width(2), .enable("false")) multiplexer_8 (
    .in0(2'b00), .in1(2'b00), .in2(2'b01), .in3(2'b10), .out(multiplexer_8_out), .sel(IROut[9:8]));
  assign OutCSel = and_74_out ? multiplexer_8_out : 2'bz;  // Controlled_Buffer controlled_buffer_46
  and and_74 (and_74_out, IROut[10], and_80_out);
  or or_60 (ARFunSel2, FETCH0, and_34_out, and_35_out);
  or or_61 (ARFunSel3, and_67_out, PUSH);
  assign ARRegSel = or_62_out ? multiplexer_5_out : 3'bz;  // Controlled_Buffer controlled_buffer_47
  or or_62 (or_62_out, and_25_out, and_68_out, and_81_out, and_86_out);
  or or_63 (ARRegSel1, FETCH0, and_36_out, BRANCH, and_69_out, and_51_out);
  or or_64 (MuxASel1, and_52_out, and_37_out);
  buf or_65 (MuxASel2, and_53_out);  // OR_Gate
  or or_66 (MuxASel3, and_54_out, and_38_out, and_55_out);
  and and_75 (and_75_out, BO, or_75_out);
  or or_67 (MuxBSel1, BRANCH, and_42_out, and_43_out);
  and and_76 (and_76_out, MOVE, FETCH);
  and and_77 (and_77_out, FETCH, PUSH);
  or or_68 (ALUFunSel1, STORE, and_45_out, and_46_out, and_12_out);
  buf or_69 (ALUFunSel4, ADD);  // OR_Gate
  buf or_70 (ALUFunSel6, and_63_out);  // OR_Gate
  assign BR = multiplexer_10_out ? 2'b01 : 2'bz;  // Controlled_Buffer controlled_buffer_48
  or or_71 (or_71_out, JMP, CALL);
  or or_72 (or_72_out, JMP, CALL);
  and and_78 (and_78_out, or_72_out, not_9_out);
  and and_79 (and_79_out, Z, JMP);
  and and_80 (and_80_out, MOVE, FETCH);
  and and_81 (and_81_out, BO, or_73_out);
  or or_73 (or_73_out, AR__GP_GP, AR__AR_GP, AR__GP_AR);
  or or_74 (ARRegSel4, PUSH, and_26_out);
  and and_82 (and_82_out, PULL, NOP0);
  or or_75 (or_75_out, GP__GP_GP, GP__AR_GP, GP__GP_AR);
  or or_76 (or_76_out, GP__GP, AR__GP);
  and and_83 (and_83_out, and_76_out, or_77_out);
  or or_77 (or_77_out, AR__AR, AR__GP);
  or or_78 (or_78_out, GP__AR, AR__AR);
  or or_79 (ALUFunSel0, and_61_out, and_30_out, and_77_out);
  buf or_80 (ALUFunSel5, and_62_out);  // OR_Gate
  _8_bit_register SBR (.CLK(CLK), .FunSel(2'b01), .E(SBRE), .I(adder_1_out), .Q(SBR_q));
  and and_84 (and_84_out, or_71_out, C);
  or or_81 (or_81_out, and_78_out, and_79_out);
  Multiplexer #(.enable("false")) multiplexer_9 (.in0(1'b1), .in1(Z), .out(C), .sel(CD_TYPE));
  and and_85 (and_85_out, FETCH, PULL);
  and and_86 (and_86_out, or_82_out, or_85_out);
  or or_82 (or_82_out, DEC, INC, MOVE);
  and and_87 (and_87_out, MOVE, FETCH, or_86_out);
  or or_83 (MuxBSel3, and_10_out, and_11_out, and_3_out);
  and and_88 (and_88_out, UO, or_78_out);
  or or_84 (MuxCSel1, and_59_out, and_60_out);
  ROM #(.dataWidth(16)) rom_1 (.addr(CAR_q), .data({F0, F1, CD_TYPE, BR_TYPE, AD}));  // open: sel
  Multiplexer #(.enable("false")) multiplexer_10 (
    .in0(and_84_out), .in1(or_81_out), .out(multiplexer_10_out), .sel(BNE));
  assign OutCSel = and_89_out ? 2'b00 : 2'bz;  // Controlled_Buffer controlled_buffer_49
  and and_89 (and_89_out, FETCH, PUSH);
  or or_85 (or_85_out, AR__GP, AR__AR);
  or or_86 (or_86_out, GP__GP, GP__AR);
  and and_90 (and_90_out, FETCH, PUSH);
  Decoder #(.select(3), .enable("false")) decoder_5 (
    .out0(GP__GP_GP), .out1(GP__AR_GP), .out2(GP__GP_AR), .out4(AR__GP_GP), .out5(AR__AR_GP),
    .out6(AR__GP_AR), .sel({IROut[10], IROut[7], IROut[4]}));  // open: out3, out7
  or or_87 (ARFunSel1, and_32_out, and_33_out, and_24_out, BRANCH, and_65_out, and_66_out, and_85_out);
  or or_88 (MuxCSel0, and_57_out, and_58_out, and_83_out, and_88_out, and_90_out);
  assign BR = RET ? 2'b10 : 2'bz;  // Controlled_Buffer controlled_buffer_50
  and and_91 (and_91_out, or_89_out, GP__GP);
  or or_89 (or_89_out, MOVE, and_92_out);
  and and_92 (and_92_out, or_90_out, NOP0);
  or or_90 (or_90_out, DEC, INC);
  assign BR = MAP ? 2'b11 : 2'bz;  // Controlled_Buffer controlled_buffer_51

  // Other names for the same wires on the sheet: I8 = IROut[8]; I9 = IROut[9]; I4 = IROut[4]; I7 = IROut[7];
  //   I10 = IROut[10]; AND = ALUFunSel7; I0 = IROut[0]; I1 = IROut[1]; I2 = IROut[2]; I3 = IROut[3]; I5 = IROut[5];
  //   I6 = IROut[6]; I11 = IROut[11]; I12 = IROut[12]; I13 = IROut[13]; I14 = IROut[14]; I15 = IROut[15];
  //   LSL = ALUFunSela; LSR = ALUFunSelb; NOT = ALUFunSel2; OR = ALUFunSel8; OutDSel0 = FETCH0

  // Notes on the sheet:
  //   GPFunSel
  //   GPFunSel0
  //   IR ENABLE
  //   IR FUNSEL
  //   OUTCSEL
  //   OutDSel
  //   ARRegSel
  //   GPFunSel1
  //   GPFunSel2
  //   GPFunSel3
  //   GPRegSel
  //   ALUFunSel
  //   ALUFunSel2
  //   ARFunSel
  //   MuxASel
  //   MuxASel0
  //   MuxASel1
  //   MuxASel2
  //   MuxASel3
  //   OutBSel
  //   MuxBSel
  //   MuxBSel0
  //   MuxBSel1
  //   MuxBSel2
  //   MuxCSel
  //   ALUFunSel0
  //   ALUFunSel1
  //   ALUFunSel4
  //   ALUFunSel5
  //   ALUFunSel6
  //   ALUFunSel7
  //   ALUFunSel8
  //   ALUFunSela
  //   ALUFunSelb
  //   OutDSel0
  //   OutDSel1
  //   OutDSel2
  //   ARRegSel0
  //   ARRegSel1
  //   ARRegSel2
  //   ARRegSel4
  //   MuxBSel3
  //   MuxCSel0
  //   MuxCSel1
  //   OutASel
  //   STR
  //   ARFunSel2
  //   ARFunSel3
  //   ARFunSel1
  //   contents of rom_1 (hex, n*v repeats v):
  //   8001 8300 126*0 4000 0 0 0 4800 0 0 0 5000 0 0 0 6800 0 0 0 d891 7000 0 0 800 0 0 0 1000 0 0 0 509d
  //   609e d000 0 50a1 58a2 d000 0 1800 0 0 0 2000 0 0 0 2800 0 0 0 3000 0 0 0 3800 0 0 0 c000 c200 0 0
  //   5b9 0 0 0 5b9 0 0 0 e8b9 0 0 0 d8c9 f000
  //   DST
  //   SRC2
  //   SRC1
endmodule
